// Logisim project hw4part1.circ as structural Verilog: 2 circuits, main circuit Register
module hw4part1 (
  input  [7:0] Input,
  input  Enable,
  output [7:0] Output
);

  wire Clock_out, Reset_out;

  Register register_1 (.Data_In(Input), .Data_Out(Output), .Clock(Clock_out), .Reset(Reset_out), .Enable(Enable));
  Clock Clock (.out(Clock_out));
  Button Reset (.out(Reset_out));

  // Notes on the sheet:
  //   You can use this to test your circuit.
endmodule

module Register (
  input  [7:0] Data_In,
  input  Clock,
  input  Reset,
  input  Enable,
  output [7:0] Data_Out
);

  D_Flip_Flop d_ff_1 (.clk(Clock), .D(Data_In[0]), .Q(Data_Out[0]), .en(Enable), .reset(Reset));  // open: Qn, preset
  D_Flip_Flop d_ff_2 (.clk(Clock), .D(Data_In[1]), .Q(Data_Out[1]), .en(Enable), .reset(Reset));  // open: Qn, preset
  D_Flip_Flop d_ff_3 (.clk(Clock), .D(Data_In[2]), .Q(Data_Out[2]), .en(Enable), .reset(Reset));  // open: Qn, preset
  D_Flip_Flop d_ff_4 (.clk(Clock), .D(Data_In[3]), .Q(Data_Out[3]), .en(Enable), .reset(Reset));  // open: Qn, preset
  D_Flip_Flop d_ff_5 (.clk(Clock), .D(Data_In[4]), .Q(Data_Out[4]), .en(Enable), .reset(Reset));  // open: Qn, preset
  D_Flip_Flop d_ff_6 (.clk(Clock), .D(Data_In[5]), .Q(Data_Out[5]), .en(Enable), .reset(Reset));  // open: Qn, preset
  D_Flip_Flop d_ff_7 (.clk(Clock), .D(Data_In[6]), .Q(Data_Out[6]), .en(Enable), .reset(Reset));  // open: Qn, preset
  D_Flip_Flop d_ff_8 (.clk(Clock), .D(Data_In[7]), .Q(Data_Out[7]), .en(Enable), .reset(Reset));  // open: Qn, preset

  // Other names for the same wires on the sheet: CLK = Clock; D[7:0] = Data_In; EN = Enable; Q[7:0] = Data_Out;
  //   RST = Reset

  // Notes on the sheet:
  //   Implement your register circuit here!
  //   My name is
  //   [Yunpeng Fan]
  //   and this is my pretty 8-bit register!
endmodule
