// Logisim project hw4part2.circ as structural Verilog: 2 circuits, main circuit One-Hot State Machine
module Tester (
  input  G
);

  wire Clock_out, one_hot_state_machine_1_w, one_hot_state_machine_1_x, one_hot_state_machine_1_y,
       one_hot_state_machine_1_z, Reset_out;

  One_Hot_State_Machine one_hot_state_machine_1 (
    .W(one_hot_state_machine_1_w), .Clock(Clock_out), .Reset(Reset_out), .G(G),
    .X(one_hot_state_machine_1_x), .Y(one_hot_state_machine_1_y), .Z(one_hot_state_machine_1_z));
  Clock Clock (.out(Clock_out));
  LED W (.in(one_hot_state_machine_1_w));
  LED X (.in(one_hot_state_machine_1_x));
  LED Y (.in(one_hot_state_machine_1_y));
  LED Z (.in(one_hot_state_machine_1_z));
  Button Reset (.out(Reset_out));

  // Notes on the sheet:
  //   You can use this to test your circuit.
endmodule

module One_Hot_State_Machine (
  input  G,
  input  Clock,
  input  Reset,
  output W,
  output X,
  output Y,
  output Z
);

  wire and_1_out, and_2_out, and_5_out, and_7_out, and_8_out, or_1_out, S0, S1, S2, S3, S4, S5, S6;
  wire [6:0] or_5_out;

  and and_1 (and_1_out, ~S0, ~S1, ~S2, ~S3, ~S4, ~S5, ~S6);  // AND_Gate
  and and_2 (and_2_out, ~G, or_1_out);  // AND_Gate
  or or_1 (or_1_out, S0, S6);
  and and_3 (or_5_out[1], G, S0);
  and and_4 (or_5_out[2], ~G, S1);  // AND_Gate
  and and_5 (and_5_out, ~G, S3);  // AND_Gate
  or or_2 (or_5_out[3], and_5_out, S2);
  and and_6 (or_5_out[4], G, S1);
  or or_3 (or_5_out[5], S4, and_7_out);
  and and_7 (and_7_out, S3, G);
  and and_8 (and_8_out, G, S6);
  or or_4 (or_5_out[6], and_8_out, S5);
  or or_5 (or_5_out[0], and_1_out, and_2_out);
  Register #(.width(7)) register_1 (
    .D(or_5_out), .Q({S6, S5, S4, S3, S2, S1, S0}), .clk(Clock), .clr(Reset));  // open: en
  or or_6 (W, S2, S3, S6);
  or or_7 (X, S0, S3);
  or or_8 (Y, S3, S5, S6);
  or or_9 (Z, S2, S4, S5);

  // Other names for the same wires on the sheet: CLK = Clock; RST = Reset

  // Notes on the sheet:
  //   My name is
  //   [Yunpeng Fan]
  //   and this is my pretty one-hot state machine!
  //   Implement your one-hot state machine circuit here!
endmodule
