// Logisim project hw4part3.circ as structural Verilog: 2 circuits, main circuit Reduced State Machine
module Tester (
  input  G
);

  wire Clock_out, reduced_state_machine_1_w, reduced_state_machine_1_x, reduced_state_machine_1_y,
       reduced_state_machine_1_z, Reset_out;

  Reduced_State_Machine reduced_state_machine_1 (
    .W(reduced_state_machine_1_w), .Clock(Clock_out), .Reset(Reset_out), .G(G),
    .X(reduced_state_machine_1_x), .Y(reduced_state_machine_1_y), .Z(reduced_state_machine_1_z));
  Clock Clock (.out(Clock_out));
  LED W (.in(reduced_state_machine_1_w));
  LED X (.in(reduced_state_machine_1_x));
  LED Y (.in(reduced_state_machine_1_y));
  LED Z (.in(reduced_state_machine_1_z));
  Button Reset (.out(Reset_out));

  // Notes on the sheet:
  //   You can use this to test your circuit.
endmodule

module Reduced_State_Machine (
  input  G,
  input  Clock,
  input  Reset,
  output W,
  output X,
  output Y,
  output Z
);

  wire and_1_out, and_2_out, and_3_out, and_4_out, and_5_out, and_6_out, and_7_out, and_8_out, and_9_out,
       and_10_out, and_11_out, and_12_out, and_13_out, and_14_out, and_15_out, and_16_out, and_17_out, S0, S2;
  wire [2:0] or_1_out;

  and and_1 (and_1_out, ~S2, W);  // AND_Gate
  and and_2 (and_2_out, S2, ~W, ~S0);  // AND_Gate
  and and_3 (and_3_out, G, ~W, ~S0);  // AND_Gate
  and and_4 (and_4_out, ~G, S0);  // AND_Gate
  and and_5 (and_5_out, S2, S0);
  and and_6 (and_6_out, ~G, ~S2, W);  // AND_Gate
  and and_7 (and_7_out, G, W, ~S0);  // AND_Gate
  and and_8 (and_8_out, S2, ~W);  // AND_Gate
  and and_9 (and_9_out, G, S0);
  and and_10 (and_10_out, G, S2);
  or or_1 (or_1_out[0], and_1_out, and_2_out, and_3_out);
  or or_2 (or_1_out[1], and_4_out, and_5_out, and_6_out, and_7_out);
  or or_3 (or_1_out[2], and_8_out, and_9_out, and_10_out);
  Register #(.width(3)) register_1 (.D(or_1_out), .Q({S2, W, S0}), .clk(Clock), .clr(Reset));  // open: en
  and and_11 (and_11_out, ~S2, ~S0, ~W);  // AND_Gate
  and and_12 (and_12_out, W, S0);
  and and_13 (and_13_out, W, S0);
  and and_14 (and_14_out, S2, S0);
  and and_15 (and_15_out, S2, W);
  and and_16 (and_16_out, S2, ~W);  // AND_Gate
  and and_17 (and_17_out, ~S2, W, ~S0);  // AND_Gate
  or or_4 (X, and_11_out, and_12_out);
  or or_5 (Y, and_13_out, and_14_out, and_15_out);
  or or_6 (Z, and_16_out, and_17_out);

  // Other names for the same wires on the sheet: S1 = W; CLK = Clock; RST = Reset

  // Notes on the sheet:
  //   Implement your reduced state machine circuit here!
  //   My name is
  //   [Yunpeng Fan]
  //   and this is my pretty reduced state machine!
endmodule
