// Logisim project timedlab1.circ as structural Verilog: 2 circuits, main circuit main
module main (
  input  RST,
  input  A
);

  wire CLK_out, statemachine_1_w, statemachine_1_x, statemachine_1_y, statemachine_1_z;

  Clock CLK (.out(CLK_out));
  LED W (.in(statemachine_1_w));
  LED Y (.in(statemachine_1_y));
  LED X (.in(statemachine_1_x));
  statemachine statemachine_1 (
    .CLK(CLK_out), .RST(RST), .A(A), .W(statemachine_1_w), .X(statemachine_1_x), .Y(statemachine_1_y),
    .Z(statemachine_1_z));
  LED Z (.in(statemachine_1_z));
endmodule

module statemachine (
  input  CLK,
  input  RST,
  input  A,
  output W,
  output X,
  output Y,
  output Z
);

  wire and_1_out, and_2_out, and_3_out, or_1_out, or_2_out, S0, S1;
  wire [4:0] or_3_out;

  and and_1 (and_1_out, ~S0, ~S1, ~X, ~Y, ~Z);  // AND_Gate
  or or_1 (or_1_out, S1, X);
  or or_2 (or_2_out, Y, S1);
  and and_2 (and_2_out, X, ~A);  // AND_Gate
  and and_3 (and_3_out, Y, A);
  or or_3 (or_3_out[0], and_1_out, Z);
  and and_4 (or_3_out[2], or_1_out, A);
  and and_5 (or_3_out[3], or_2_out, ~A);  // AND_Gate
  or or_4 (or_3_out[4], and_2_out, and_3_out);
  Register #(.width(5)) register_1 (
    .D({or_3_out[4:2], S0, or_3_out[0]}), .Q({Z, Y, X, S1, S0}), .clk(CLK), .clr(RST));  // open: en
  or or_5 (W, S1, Z);

  // Other names for the same wires on the sheet: S2 = X; S3 = Y; S4 = Z

  // Notes on the sheet:
  //   Hello! My name is 
  //   <Yunpeng Fan>
  //   And this is my pretty state machine!
endmodule
